# Fritzing sketch tarefa-02 (saved by Fritzing 0.9.3b)
breadboards: 1

parts:
  Componente1 = Arduino Uno (Rev3) - ICSP
  R6 = Resistor [tolerance=±5% resistance=220 package=THT]
  R4 = Resistor [tolerance=±5% resistance=220 package=THT]
  R5 = Resistor [tolerance=±5% resistance=220 package=THT]
  Componente2 = Bluetooth HC-05 Macho  # not connected
  R3 = Resistor [tolerance=±5% resistance=330 package=THT]
  R1 = Resistor [tolerance=±5% resistance=330 package=THT]
  R2 = Resistor [tolerance=±5% resistance=330 package=THT]
  LED1 = RGB LED - (4 legs) [package="5 mm [THT]"]
  TTP223B1 = TTP223B Capacitive Touch Sensor Module
  LCD1 = LCD screen
  LCM1602_IIC1 = LCM1602 IIC [part_number="LCM1602 IIC" chip_label="LCM1602 IIC" package="DIP (Dual Inline) [THT]"]

nets:
  VCC: Componente1.A3, Componente1.A4/SDA, Componente1.5V, R4.Pin_0, LED1.common_anode, TTP223B1.VCC, LCM1602_IIC1.VCC, LCM1602_IIC1.SDA, LCM1602_IIC1.SCL
  GND: Componente1.GND, TTP223B1.GND, LCM1602_IIC1.GND
  N1: Componente1.D10_PWM/SS, R6.Pin_1
  N2: Componente1.D12/MISO, TTP223B1.SIG
  N3: Componente1.D3_PWM, R1.Pin_1
  N4: Componente1.D4, R2.Pin_1
  N5: Componente1.D5_PWM, R3.Pin_1
  N6: R6.Pin_0, R5.Pin_1
  N7: R4.Pin_1, R5.Pin_0
  N8: R3.Pin_0, LED1.blue_cathode
  N9: R1.Pin_0, LED1.red_cathode
  N10: R2.Pin_0, LED1.green_cathode
  VSS: LCD1.VSS, LCM1602_IIC1.VSS
  VDD: LCD1.VDD, LCM1602_IIC1.VDD
  N11: LCD1.V0, LCM1602_IIC1.V0
  N12: LCD1.RS, LCM1602_IIC1.RS
  N13: LCD1.R/W, LCM1602_IIC1.RW
  N14: LCD1.E, LCM1602_IIC1.E
  N15: LCD1.DB0, LCM1602_IIC1.D0
  N16: LCD1.DB1, LCM1602_IIC1.D1
  N17: LCD1.DB2, LCM1602_IIC1.D2
  N18: LCD1.DB3, LCM1602_IIC1.D3
  N19: LCD1.DB4, LCM1602_IIC1.D4
  N20: LCD1.DB5, LCM1602_IIC1.D5
  N21: LCD1.DB6, LCM1602_IIC1.D6
  N22: LCD1.DB7, LCM1602_IIC1.D7
  N23: LCD1.LED+, LCM1602_IIC1.A
  N24: LCD1.LED-, LCM1602_IIC1.K
  N25: LCM1602_IIC1.LED_A, LCM1602_IIC1.LED_B

custom parts:
  TTP223B Capacitive Touch Sensor Module: The TTP223B capacitive touch sensor module uses the TTP223B IC. The appropriate voltage is approximately 2 to 5.5 volts.
  LCM1602 IIC: I2C-Module to use a 1602 or 2004 LCD on with the wire.h libory Serial LCD Modul
